# Fritzing sketch client_LED (saved by Fritzing 0.9.3b)
circuit board: 8.46667cm x 5.64444cm
breadboards: 1

parts:
  Light_2 = LED - 5mm [color="Blue (505nm)" package="5 mm [THT]"]
  U2 = 2-Channel 5v Relay Shield [package=relay-2ch5v10a]
  U1 = NodeMCU V3.0
  Light1 = LED - 5mm [color="Red (633nm)" package="5 mm [THT]"]

nets:
  N1: Light_2.cathode, U2.GND, U1.GND#6, U1.GND#13, U1.GND#16, U1.GND#33, Light1.cathode
  N2: Light_2.anode, U1.D5
  VCC: U2.VCC, U1.3V3
  N3: U2.IN1, U1.D1
  N4: U2.IN2, U1.D2
  N5: U1.D6, Light1.anode

custom parts:
  2-Channel 5v Relay Shield: 2 Channel 5v Relay Shield w. 2x SPD-06VDC-SD-C
  NodeMCU V3.0: ESP8266 based NodeMCU

// code stored in the sketch: client_socket.ino
#include <ESP8266WiFi.h>
#include <SocketIOClient.h>
 
SocketIOClient client;
const char* ssid = "Thao";
const char* password = "87488987";
 
const char* host = "https://smarthome2018.herokuapp.com";
extern String RID;
extern String Rfull;
 
void setup(){
    //B?t baudrate ? m?c 115200 ?? giao ti?p v?i máy tính qua Serial
    Serial.begin(115200);
    delay(10);
 
    //Vi?c ??u tiên c?n làm là k?t n?i vào m?ng Wifi
    Serial.print("Ket noi vao mang ");
    Serial.println(ssid);
 
    //K?t n?i vào m?ng Wifi
    WiFi.begin(ssid, password);
 
    //Ch? ??n khi ?ã ???c k?t n?i
    while (WiFi.status() != WL_CONNECTED) { //Thoát ra kh?i vòng 
        delay(500);
        Serial.print('.');
    }
 
    Serial.println();
    Serial.println(F("Da ket noi WiFi"));
    Serial.println(F("Di chi IP cua ESP8266 (Socket Client ESP8266): "));
    Serial.println(WiFi.localIP());
 
    if (!client.connect(host, port)) {
        Serial.println(F("Ket noi den socket server that bai!"));
        return;
    }
 
    if (client.connected()) {
        client.send("connection", "message", "Connected !!!!");
    }
}
 
void loop(){
    //t?o m?t task c? sau "interval" giây thì ch?y l?nh:
    if (millis() - previousMillis > interval) {
        //l?nh:
        previousMillis = millis();
 
        //g?i s? ki?n "atime" là m?t JSON ch?a tham s? message có n?i dung là Time please?
        client.send("atime", "message", "Time please?");
    }
 
    //Khi b?t ???c b?t k? s? ki?n nào thì chúng ta có hai tham s?:
    //  +RID: Tên s? ki?n
    //  +RFull: Danh sách tham s? ???c nén thành chu?i JSON!
    if (client.monitor()) {
        Serial.println(RID);
        Serial.println(Rfull);
    }

    if (!client.connected()) {
      client.reconnect(host, port);
    }
}
