# Fritzing sketch 1relay_compact_v1.0 (saved by Fritzing 0.9.3b)
circuit board: 4.9cm x 4.86cm
breadboards: 1

parts:
  U1 = atmega328 [package=dip]
  Part1 = NRF24L01+ Breakout Board  # not connected
  JP1 = Header 4 [package=molex-1x4_lock]
  Q1 = NPN-Transistor [part_number=2N2222A package="TO92 [THT]"]
  R1 = Resistor upright [tolerance=±5% resistance=1k package=THT]
  IC1 = Voltage Regulator LM1117 [package=sot223]
  OMRON1 = OMRON PCB Power Relay – G5LE [part_number=JQC-3F(T73) package=THT]
  JP4 = Header 1 [package=1x01_offset]
  Y1 = Resonator [frequency="16 Mhz" package=THT]
  R2 = Resistor upright [tolerance=±5% resistance=1M package=THT]
  C3 = Capacitor Polarized [package=cpol-radial-10uf-25v]
  JP6 = Header 8 smd 1.27 [part_number="nRF24L01 SMD" package="8 pads 1.27mm"]
  D1 = Diode upright [part_number=1N4001 package=diode-1n4001]
  HLK-PM3 = HLK-PM01_ch
  J3 = screw terminal, 3 pins
  J7 = screw terminal, 3 pins
  J5 = screw terminal, 2 pins
  J4 = screw terminal, 4 pins
  J6 = screw terminal, 3 pins
  J8 = screw terminal, 2 pins
  J9 = screw terminal, 3 pins

nets:
  N1: U1.D0_(RX), JP1.4
  N2: U1.D1_(TX), JP1.3
  N3: U1.D2, R1.Pin_1
  N4: U1.D3_(PWM), J5.pin2
  N5: U1.D4, J5.pin1
  N6: U1.VCC, U1.AVCC, JP1.2, IC1.IN, OMRON1.COIL1, D1.C, J3.pin3
  GND: U1.GND, JP1.1, Q1.E, IC1.ADJ, Y1.GND, C3.-, JP6.8, HLK-PM3.-Vo, J3.pin2
  N7: U1.XLAT1, Y1.0, R2.Pin_0
  N8: U1.XLAT2, Y1.pin_1, R2.Pin_1
  N9: U1.D5_(PWM), J4.pin4
  N10: U1.D6_(PWM), J4.pin3
  N11: U1.D7, J4.pin2
  N12: U1.D8, J4.pin1
  N13: U1.D9_(PWM), JP6.2
  N14: U1.D10_(PWM), JP6.3
  N15: U1.D11_(PWM), JP6.5
  N16: U1.D12, JP6.6
  N17: U1.D13, JP6.4
  N18: U1.A0, J7.pin3
  N19: U1.A1, J7.pin2
  N20: U1.A2, J7.pin1
  N21: U1.A3, J6.pin1
  N22: U1.A4, J6.pin2
  N23: U1.A5, J6.pin3
  N24: Q1.B, R1.Pin_0
  N25: Q1.C, OMRON1.COIL2, D1.A
  N26: IC1.OUT, C3.+, JP6.1, J3.pin1
  N27: OMRON1.A, J9.pin1
  N28: OMRON1.C, J9.pin3
  N29: OMRON1.B, J9.pin2
  N30: JP4.1, HLK-PM3.+Vo
  N31: HLK-PM3.AC#0, J8.pin1
  N32: HLK-PM3.AC#1, J8.pin2

notes:
  nRF24l01+ micro with SMD header
  +3.3V
  GND
  +5V
  D8
  D7
  D6
  D3
  D4
  A4
  A3
  A5
  D5
  1relay_compact_v1.0
  180121 by PowerPenguin
  Multi-purpose MySensor Node for wall
  socket/switch integration based on
  ATmega328p and nRF24L01
  Vcc
  RX
  TX

custom parts:
  Resistor upright: A generic upright standing resistor (0.25W)
  Header 8 smd 1.27: Header 8 smd with 1.27 mm pitch (for micro nRF24l01+ module
  Diode upright: Diode These are standard reverse protection diodes and small signal diodes. SMA package can handle up to about 1A. SOD-323 can handle about 200mA. What the SOD-323 package when ordering, there are some mfgs out there that are 5-pin packages.
  HLK-PM01_ch: AC-DC 220V to 5V Step-Down Power Supply Module PCB holes much too small -- corrected 180121 by ppenguin

// code stored in the sketch: 1relay_compact_v1.0.ino
/**
 * The MySensors Arduino library handles the wireless radio link and protocol
 * between your home built sensors/actuators and HA controller of choice.
 * The sensors forms a self healing radio network with optional repeaters. Each
 * repeater and gateway builds a routing tables in EEPROM which keeps track of the
 * network topology allowing messages to be routed to nodes.
 *
 * Created by Henrik Ekblad <henrik.ekblad@mysensors.org>
 * Copyright (C) 2013-2015 Sensnology AB
 * Full contributor list: https://github.com/mysensors/Arduino/graphs/contributors
 *
 * Documentation: http://www.mysensors.org
 * Support Forum: http://forum.mysensors.org
 *
 * This program is free software; you can redistribute it and/or
 * modify it under the terms of the GNU General Public License
 * version 2 as published by the Free Software Foundation.
 *
 *******************************
 *
 * REVISION HISTORY
 * Version 1.0 - Henrik Ekblad
 *
 * DESCRIPTION
 * Example sketch showing how to control physical relays.
 * This example will remember relay state after power failure.
 * http://www.mysensors.org/build/relay
 */

// Enable debug prints to serial monitor
#define MY_DEBUG

// Enable and select radio type attached
#define MY_RADIO_NRF24
//#define MY_RADIO_RFM69

// Enable repeater functionality for this node
#define MY_REPEATER_FEATURE

#include <MySensors.h>

#define RELAY_1  2  // Arduino Digital I/O pin number for first relay (second on pin+1 etc)
#define NUMBER_OF_RELAYS 1 // Total number of attached relays
#define RELAY_ON 1  // GPIO value to write to turn on attached relay
#define RELAY_OFF 0 // GPIO value to write to turn off attached relay


void before()
{
	for (int sensor=1, pin=RELAY_1; sensor<=NUMBER_OF_RELAYS; sensor++, pin++) {
		// Then set relay pins in output mode
		pinMode(pin, OUTPUT);
		// Set relay to last known state (using eeprom storage)
		digitalWrite(pin, loadState(sensor)?RELAY_ON:RELAY_OFF);
	}
}

void setup()
{

}

void presentation()
{
	// Send the sketch version information to the gateway and Controller
	sendSketchInfo("Relay", "1.0");

	for (int sensor=1, pin=RELAY_1; sensor<=NUMBER_OF_RELAYS; sensor++, pin++) {
		// Register all sensors to gw (they will be created as child devices)
		present(sensor, S_BINARY);
	}
}


void loop()
{

}

void receive(const MyMessage &message)
{
	// We only expect one type of message from controller. But we better check anyway.
	if (message.type==V_STATUS) {
		// Change relay state
		digitalWrite(message.sensor-1+RELAY_1, message.getBool()?RELAY_ON:RELAY_OFF);
		// Store state in eeprom
		saveState(message.sensor, message.getBool());
		// Write some debug info
		Serial.print("Incoming change for sensor:");
		Serial.print(message.sensor);
		Serial.print(", New status: ");
		Serial.println(message.getBool());
	}
}
